# Fritzing sketch NodeMCUWeatherStation (saved by Fritzing 0.9.6b)
circuit board: 12.5cm x 5.5cm
breadboards: 1

parts:
  Module_1 = Robotdyn MAX7219 8x8 LedMatrix Module
  R1 = TRIMPOT [package=trim_pot_pth]
  Module_2 = Robotdyn MAX7219 8x8 LedMatrix Module
  NodeMCU = ESP8266 NodeMCU LoLin module
  LED2 = LED - 3mm [color="Yellow (585nm)" current=0.030 package="3 mm [THT]"]
  LED1 = LED - 3mm [color="Green (565nm)" current=0.030 package="3 mm [THT]"]
  R2 = Resistor [tolerance=±5% resistance=4.7k power=0.25 package=THT]
  R3 = Resistor [tolerance=±5% resistance=100 power=0.25 package=THT]
  R4 = Resistor [tolerance=±5% resistance=100 power=0.25 package=THT]
  J1 = Power Jack [package=power_jack_slot]
  Module_3 = Robotdyn MAX7219 8x8 LedMatrix Module

nets:
  N1: Module_1.5V-in, Module_1.5V-out, Module_2.5V-in, Module_2.5V-out, NodeMCU.Vin, J1.PWR, Module_3.5V-in, Module_3.5V-out
  GND: Module_1.GND-in, Module_1.GND-out, R1.CCW, Module_2.GND-in, Module_2.GND-out, NodeMCU.GND, R3.Pin_0, R4.Pin_0, J1.GND, Module_3.GND-in, Module_3.GND-out
  N2: Module_1.CS-in, Module_1.CS-out, Module_2.CS-in, Module_2.CS-out, NodeMCU.D8, Module_3.CS-in, Module_3.CS-out
  N3: Module_1.SCL-in, Module_1.SCL-out, Module_2.SCL-in, Module_2.SCL-out, NodeMCU.D5, Module_3.SCL-in, Module_3.SCL-out
  N4: Module_1.SDI-in, NodeMCU.D7
  N5: Module_1.SDO-out, Module_2.SDI-in
  N6: R1.WIPER, NodeMCU.A0
  N7: R1.CW, NodeMCU.3V3, R2.Pin_1
  N8: Module_2.SDO-out, Module_3.SDI-in
  N9: NodeMCU.D1, LED1.anode
  N10: NodeMCU.D2, LED2.anode
  N11: NodeMCU.D3, R2.Pin_0, J1.GNDBREAK
  N12: LED2.cathode, R3.Pin_1
  N13: LED1.cathode, R4.Pin_1

notes:
  JLCJLCJLCJLC
  NodeMCU Weather Station
  v4
  NodeMCU Weather Station, https://github.com/otherguy/NodeMCUWeatherStation, 4

custom parts:
  Robotdyn MAX7219 8x8 LedMatrix Module: Description: Robotdyn MAX7219 8x8 LedMatrix Module (various colors available) Dimensions: 32x32mm Documents:
  ESP8266 NodeMCU LoLin module: ESP8266 based NodeMCU
